// Logisim project projetos.circ as structural Verilog: 6 circuits, main circuit main
module main (
  input  in_1,
  input  in_2,
  input  [3:0] in_3,
  input  [3:0] in_4,
  input  [3:0] in_5,
  input  in_6,
  input  [3:0] in_7,
  input  [3:0] in_8,
  output out_9,
  output out_10,
  output out_11,
  output [3:0] out_12,
  output [3:0] out_13,
  output [3:0] out_14
);

  add_1 ADD1 (.S(out_11), .vai_1(out_9), .A(in_1), .B(in_2), .vem_1(in_6));
  Sub sub_1 (.A(in_7), .B(in_8), .resultado(out_14));
  add_4 ADD4 (.in_2(in_3), .in_1(in_4), .out_4(out_12), .Overflow(out_10));
  complemento_de_2 complemento_de_2_1 (.in_1(in_5), .out_2(out_13));
endmodule

module add_1 (
  input  A,
  input  B,
  input  vem_1,
  output S,
  output vai_1
);

  wire and_1_out, and_2_out, or_1_out, xor_1_out;

  xor xor_1 (xor_1_out, B, A);
  or or_1 (or_1_out, vem_1, B);
  and and_1 (and_1_out, B, vem_1);
  xor xor_2 (S, vem_1, xor_1_out);
  and and_2 (and_2_out, or_1_out, A);
  or or_2 (vai_1, and_2_out, and_1_out);
endmodule

module add_4 (
  input  [3:0] in_1,
  input  [3:0] in_2,
  output Overflow,
  output [3:0] out_4
);

  wire add_1_2_vai_1, add_1_3_vai_1, add_1_4_vai_1;

  add_1 ADD_1 (.S(out_4[3]), .vai_1(Overflow), .A(in_2[3]), .B(in_1[3]), .vem_1(add_1_2_vai_1));
  add_1 add_1_2 (.S(out_4[2]), .vai_1(add_1_2_vai_1), .A(in_2[2]), .B(in_1[2]), .vem_1(add_1_3_vai_1));
  add_1 add_1_3 (.S(out_4[1]), .vai_1(add_1_3_vai_1), .A(in_2[1]), .B(in_1[1]), .vem_1(add_1_4_vai_1));
  add_1 add_1_4 (.S(out_4[0]), .vai_1(add_1_4_vai_1), .A(in_2[0]), .B(in_1[0]), .vem_1(1'b0));
endmodule

module add_8 (
  input  [3:0] in_1,
  input  [3:0] in_2,
  output out_3,
  output [3:0] out_4
);

  // Probe on in_1
  add_4 add_4_1 (.in_2(in_1), .in_1(in_2), .out_4(out_4), .Overflow(out_3));
  // Probe on out_4
  // Probe on in_2
endmodule

// COMP
module complemento_de_2 (
  input  [3:0] in_1,
  output [3:0] out_2
);

  wire [3:0] not_4_out;

  not not_1 (not_4_out[3], in_1[3]);
  not not_2 (not_4_out[1], in_1[1]);
  not not_3 (not_4_out[2], in_1[2]);
  not not_4 (not_4_out[0], in_1[0]);
  add_4 add_4_1 (.in_2(not_4_out), .in_1(4'b0001), .out_4(out_2));  // open: Overflow
endmodule

// SUB
module Sub (
  input  [3:0] A,
  input  [3:0] B,
  output [3:0] resultado
);

  wire [3:0] complemento_de_2_1_out_2;

  add_4 ADD4 (.in_2(A), .in_1(complemento_de_2_1_out_2), .out_4(resultado));  // open: Overflow
  complemento_de_2 complemento_de_2_1 (.in_1(B), .out_2(complemento_de_2_1_out_2));
endmodule
